# Fritzing sketch skematik (saved by Fritzing 0.9.3b)

parts:
  MH-ET_LIVE_ESP32_DEVKIT1 = MH-ET LIVE ESP32 DEVKIT 38 pins
  DS1 = DS18B20 1-Wire Temperature Sensor Probe
  J1 = Basic Servo
  Part1 = LCD1602-I2C
  LED1 = LED - 5mm [color="Red (633nm)" package="5 mm [THT]"]
  R3 = Resistor [tolerance=±5% resistance=4.7k package=THT]
  R2 = Resistor [tolerance=±5% resistance=220 package=THT]

nets:
  3V3: MH-ET_LIVE_ESP32_DEVKIT1.3V3, DS1.VDD, R3.Pin_0
  N1: MH-ET_LIVE_ESP32_DEVKIT1.IO27, R2.Pin_0
  N2: MH-ET_LIVE_ESP32_DEVKIT1.GND#58, DS1.GND, LED1.cathode
  N3: MH-ET_LIVE_ESP32_DEVKIT1.IO13, J1.pulse
  VCC: MH-ET_LIVE_ESP32_DEVKIT1.5V, J1.vcc, Part1.VCC
  GND: MH-ET_LIVE_ESP32_DEVKIT1.GND#64, J1.gnd, Part1.GND
  N4: MH-ET_LIVE_ESP32_DEVKIT1.IO22, Part1.SCL
  N5: MH-ET_LIVE_ESP32_DEVKIT1.IO21, Part1.SDA
  N6: MH-ET_LIVE_ESP32_DEVKIT1.IO4, DS1.DQ, R3.Pin_1
  N7: LED1.anode, R2.Pin_1

custom parts:
  MH-ET LIVE ESP32 DEVKIT 38 pins: http://mh.nodebb.com/topic/2/mh-et-live-esp32-devkit
  LCD1602-I2C: A standard character display, usually with 2x16 characters. Comes in many colors with LCM1602 IIC attached.
